# Fritzing sketch fritzing (saved by Fritzing 1.0.3b)
breadboards: 1

parts:
  Mod1 = Raspberry Pi 4B
  Power_plug1 = Power plug
  8x8_LED_Modul_mit_MAX1 = 8x8 LED Modul mit MAX7219 [package=THT]
  New_Part2 = MCP23017 [package="DIP (Dual Inline) [THT]"]

nets:
  N1: Mod1.GPIO2, New_Part2.SCL
  N2: Mod1.GPIO3, New_Part2.SDA
  GND: Mod1.GND, Power_plug1.GND, New_Part2.GND, New_Part2.A0, New_Part2.A1, New_Part2.A2
  VCC: Power_plug1.VCC, 8x8_LED_Modul_mit_MAX1.VCC_Eingang, New_Part2.VCC, New_Part2.RST

notes:
  5V external power supply
  Here a 8x 7 segment module
  https://www.az-delivery.de/products/azdelivery-max7219-led-modul-8-bit-7-segmentanzeige-led-display-fur-arduino-und-raspberry-pi
  Opto & LED hier für Licht AN/AUS

custom parts:
  MCP23017: 16 bit I/O chip controlled via I2C
